# Fritzing sketch lab5 (saved by Fritzing 0.9.1b)
breadboards: 4

parts:
  Part1 = Arduino Nano (Rev3.0)
  T1 = LM35 Temperature Sensor [package="TO92 [THT]"]
  U2 = HC-SR04 [chip_label=IC package="SIP (Single Inline) [THT]"]
  A4988 = 74HC139N [part_number=A4988 package="DIP (Dual Inline) [THT]"]
  C2 = Capacitor Polarized [package=cpol-radial-100uf-25v]
  M1 = Stepper Motor - Bipolar

nets:
  GND: Part1.GND, T1.GND, U2.GND, A4988.2Y3
  N1: Part1.D2, A4988.GND
  N2: Part1.D3, A4988.1Y3
  N3: Part1.D4, A4988.1Y2
  N4: Part1.D5, A4988.1Y1
  N5: Part1.D6, A4988.1G_
  N6: Part1.D7, U2.Trig
  N7: Part1.D8, U2.Echo
  5V: Part1.5V, T1.+Vs, U2.Vcc, A4988.2Y2
  N8: Part1.A0, T1.Vout
  N9: A4988.2Y1, M1.D
  N10: A4988.2Y0, M1.B
  N11: A4988.2B, M1.C
  N12: A4988.2A, M1.A
  N13: A4988.2G_, C2.-
  N14: A4988.VCC, C2.+

notes:
  Ultrasonic sensor pins labels are backwards since component does not flip.
  These power and ground wires connect to external 12V source used needed by stepper motor.

custom parts:
  HC-SR04: HC-SR04 ultrasound distance sensor
